# Fritzing sketch Arduino_Uploader (saved by Fritzing 0.9.2b)
circuit board: 8.46667cm x 5.64444cm
breadboards: 1

parts:
  U1 = ESP8266 WiFi Module [part_number=ESP8266]
  Parte1 = Arduino Uno (Rev3)
  S1 = Momentary Switch [package=ksa_sealed_tac_switch]
  R1 = Resistor [tolerance=±5% resistance=330 package=THT]
  LED1 = LED - 5mm [color="Red (633nm)" package="5 mm [THT]"]

nets:
  N1: U1.IO0, Parte1.D2
  N2: U1.IO2, R1.Pin_1
  N3: U1.RST, S1.3
  N4: U1.CHIP_EN, Parte1.D3_PWM
  N5: U1.IO15, U1.GND#23, Parte1.GND, S1.1, LED1.cathode
  N6: U1.TX, Parte1.D1/TX
  N7: U1.RX, Parte1.D0/RX
  N8: U1.3.3V#26, Parte1.3V3
  N9: R1.Pin_0, LED1.anode

// code stored in the sketch: ArduinoAsESP8266_Uploader.ino
//Sketch to upload new firmware or new skecthes to ESP8266
//Note: RX<=>RX TX<=>TX Put after the upload the main sketch
//sketch para cargar un nuevo firmware o sketch a ESP8266 por medio de Arduino
//Nota: RX<=>RX TX<=>TX Colocarlos depsues de cargar el Sketch
//Source-Fuente: http://www.instructables.com/id/Cargar-firmware-al-ESP8266-con-Arduino/?ALLSTEPS
int ch_pd = 3; 
int io0 = 2; //GPIO0

void setup() {
  pinMode(ch_pd, OUTPUT);
  pinMode(io0, OUTPUT);
  digitalWrite(io0,LOW);
  digitalWrite(ch_pd, LOW);
  delay(1000);
  digitalWrite(ch_pd, HIGH);
}

void loop()
{
      
}
